// Logisim project Computer_8bit.circ as structural Verilog: 12 circuits, main circuit main
module main (
  input  in_1,
  input  in_2,
  input  in_3,
  input  in_4,
  input  in_5,
  input  in_6,
  input  [6:0] in_7,
  input  in_8,
  input  in_9,
  input  [8:0] in_10,
  input  [8:0] in_11,
  input  [7:0] in_12,
  input  [23:0] in_13,
  input  [23:0] in_14,
  input  [7:0] in_15,
  input  in_16,
  input  in_17,
  input  in_18,
  output [7:0] out_19,
  output out_20
);

  wire characterwriter_1_char1, characterwriter_1_char2, CLK, clock_2_out, tsegab_cpu_1_clk, tsegab_cpu_1_oe,
       tsegab_cpu_1_we, vram_1_clk, vram_1_rst, vram_1_we;
  wire [7:0] counter_1_q;
  wire [8:0] vram_1_x, vram_1_y;
  wire [13:0] ram_2_dout;
  wire [23:0] characterwriter_1_value_out, Memory_ADDR, vram_1_rgb;
  wire [31:0] ram_1_dout, tsegab_cpu_1_memory_value;

  Tsegab_CPU tsegab_cpu_1 (
    .PC_COUNTER_RST(in_9), .CPU_INIT(in_8), .CPU_RST(in_1), .RESET_REG(in_1), .MEM_OUT(ram_1_dout),
    .CPU_CLK(CLK), .WE(tsegab_cpu_1_we), .OE(tsegab_cpu_1_oe), .CLK(tsegab_cpu_1_clk),
    .Memory_VALUE(tsegab_cpu_1_memory_value), .Memory_ADDR(Memory_ADDR));  // open: ADDR, DATA, Write_Enable, CPU_OUT, T1CLK, T2CLK, T3CLK, T4CLK
  RAM #(.addrWidth(24), .dataWidth(32)) ram_1 (
    .addr(Memory_ADDR), .we(tsegab_cpu_1_we), .oe(tsegab_cpu_1_oe), .clk(tsegab_cpu_1_clk),
    .din(tsegab_cpu_1_memory_value), .dout(ram_1_dout));
  Clock clock_1 (.out(CLK));
  // Telnet telnet_1: pin names not known; wires that end beside it: in_15, in_16, in_18, out_19, out_20, in_17
  CharacterWriter characterwriter_1 (
    .CLK(CLK), .RST(in_1), .CX(vram_1_x), .CY(vram_1_y), .UX(in_10), .UY(in_11), .Letter(in_12), .BG(in_13),
    .FG(in_14), .VALUE_OUT(characterwriter_1_value_out), .CHAR1(characterwriter_1_char1),
    .CHAR2(characterwriter_1_char2));
  VRAM vram_1 (
    .CHAR1(characterwriter_1_char1), .CHAR2(characterwriter_1_char2), .CLK_IN(CLK), .WE_PORT_IN(in_2),
    .RST_IN(in_1), .VALUE_IN(characterwriter_1_value_out), .RST(vram_1_rst), .CLK(vram_1_clk),
    .WE(vram_1_we), .X(vram_1_x), .Y(vram_1_y), .RGB(vram_1_rgb));
  // RGB_Video #(.height(512), .scale(1), .width(512)) rgb_video_1: pin names not known; wires that end beside it: vram_1_rst, vram_1_clk, vram_1_we, vram_1_x, vram_1_y, vram_1_rgb
  Clock clock_2 (.out(clock_2_out));
  Counter counter_1 (.clr(in_5), .up(in_6), .count(in_6), .clk(clock_2_out), .Q(counter_1_q));  // open: load, D, carry
  RAM #(.dataWidth(14)) ram_2 (.addr(counter_1_q), .oe(in_6), .clk(clock_2_out), .dout(ram_2_dout));  // open: we, din
  // Buzzer buzzer_1: pin names not known; wires that end beside it: ram_2_dout, in_3, in_7

  // Other names for the same wires on the sheet: OE = in_4; RST = in_1; WE = in_2
endmodule

module ALU (
  input  [7:0] in_1,
  input  [7:0] in_2,
  input  ADD,
  input  SUB,
  input  MUL,
  input  CMP,
  output [7:0] out_7,
  output GREATER_FRST,
  output EQUAL,
  output GREATER_SECOND
);

  wire comparator_1_eq, comparator_1_gt, comparator_1_lt;
  wire [7:0] adder_1_out, multiplier_1_out, subtractor_1_out;

  Adder adder_1 (.a(in_1), .b(in_2), .out(adder_1_out));  // open: cin, cout
  Subtractor subtractor_1 (.a(in_1), .b(in_2), .out(subtractor_1_out));  // open: bin, bout
  Multiplier multiplier_1 (.a(in_1), .b(in_2), .out(multiplier_1_out));  // open: cin, cout
  Comparator comparator_1 (.a(in_1), .b(in_2), .gt(comparator_1_gt), .eq(comparator_1_eq), .lt(comparator_1_lt));
  assign out_7 = ADD ? adder_1_out : 8'bz;  // Controlled_Buffer controlled_buffer_1
  assign out_7 = SUB ? subtractor_1_out : 8'bz;  // Controlled_Buffer controlled_buffer_2
  assign GREATER_FRST = CMP ? comparator_1_gt : 1'bz;  // Controlled_Buffer controlled_buffer_3
  assign EQUAL = CMP ? comparator_1_eq : 1'bz;  // Controlled_Buffer controlled_buffer_4
  assign GREATER_SECOND = CMP ? comparator_1_lt : 1'bz;  // Controlled_Buffer controlled_buffer_5
  assign out_7 = MUL ? multiplier_1_out : 8'bz;  // Controlled_Buffer controlled_buffer_6
endmodule

module OneHot_Counter (
  input  INT,
  input  CLK,
  input  RST,
  output [5:0] out_4
);

  D_Flip_Flop d_ff_1 (.D(out_4[5]), .clk(CLK), .Q(out_4[0]), .preset(INT), .reset(RST));  // open: Qn
  D_Flip_Flop d_ff_2 (.D(out_4[0]), .clk(CLK), .Q(out_4[1]), .reset(RST));  // open: Qn, preset
  D_Flip_Flop d_ff_3 (.D(out_4[1]), .clk(CLK), .Q(out_4[2]), .reset(RST));  // open: Qn, preset
  D_Flip_Flop d_ff_4 (.D(out_4[2]), .clk(CLK), .Q(out_4[3]), .reset(RST));  // open: Qn, preset
  D_Flip_Flop d_ff_5 (.D(out_4[3]), .clk(CLK), .Q(out_4[4]));  // open: Qn, preset, reset
  D_Flip_Flop d_ff_6 (.D(out_4[4]), .clk(CLK), .Q(out_4[5]));  // open: Qn, preset, reset
endmodule

module PC_Counter (
  input  LOAD_DATA,
  input  CLK,
  input  [23:0] DATA,
  input  CLR,
  output [23:0] ADDR
);

  Counter #(.max('hffffff), .width(24)) counter_1 (
    .clr(CLR), .load(LOAD_DATA), .count(CLK), .clk(CLK), .D(DATA), .Q(ADDR));  // open: up, carry
endmodule

module OPTCODE_INENT (
  input  [3:0] OPTCODE,
  output STR_C,
  output LDA_C,
  output JL_C,
  output JG_C,
  output JNE_C,
  output JE_C,
  output CMP_C,
  output JMP_C,
  output HLT_C,
  output OUT_C,
  output MOV_C,
  output MUL_C,
  output SUB_C,
  output ADD_C,
  output NOP_C
);

  wire not_1_out, not_2_out, not_3_out, not_4_out;

  not not_1 (not_1_out, OPTCODE[0]);
  not not_2 (not_2_out, OPTCODE[1]);
  not not_3 (not_3_out, OPTCODE[2]);
  not not_4 (not_4_out, OPTCODE[3]);
  and STR (STR_C, OPTCODE[3], OPTCODE[2], OPTCODE[1], not_1_out);
  and LDA (LDA_C, OPTCODE[3], OPTCODE[2], not_2_out, OPTCODE[0]);
  and JL (JL_C, OPTCODE[3], OPTCODE[2], not_2_out, not_1_out);
  and JG (JG_C, OPTCODE[3], not_3_out, OPTCODE[1], OPTCODE[0]);
  and JNE (JNE_C, OPTCODE[3], not_3_out, OPTCODE[1], not_1_out);
  and JE (JE_C, OPTCODE[3], not_2_out, not_3_out, OPTCODE[3]);
  and CMP (CMP_C, OPTCODE[3], not_3_out, not_2_out, not_1_out);
  and JMP (JMP_C, OPTCODE[0], OPTCODE[1], OPTCODE[2], OPTCODE[3]);
  and HLT (HLT_C, OPTCODE[0], OPTCODE[1], OPTCODE[2], not_4_out);
  and OTPT (OUT_C, not_1_out, OPTCODE[1], OPTCODE[2], not_4_out);
  and MOV (MOV_C, OPTCODE[0], not_2_out, OPTCODE[2], not_4_out);
  and MUL (MUL_C, OPTCODE[0], OPTCODE[1], not_3_out, not_4_out);
  and SUB (SUB_C, not_1_out, OPTCODE[1], not_3_out, not_4_out);
  and ADD (ADD_C, OPTCODE[0], not_2_out, not_3_out, not_4_out);
  and NOP (NOP_C, not_4_out, not_3_out, not_2_out, not_1_out);
endmodule

module REG_IDENT (
  input  [3:0] REGSTER_NUM,
  output [7:0] REG_OUT
);

  ROM #(.addrWidth(4)) rom_1 (.addr(REGSTER_NUM), .data(REG_OUT));

  // Notes on the sheet:
  //   contents of rom_1 (hex, n*v repeats v):
  //   0 1 2 4 8 10 20 40 80
endmodule

module Tsegab_CPU (
  input  CPU_INIT,
  input  CPU_CLK,
  input  CPU_RST,
  input  PC_COUNTER_RST,
  input  Write_Enable,
  input  [23:0] ADDR,
  input  [40:0] DATA,
  input  [31:0] MEM_OUT,
  input  RESET_REG,
  output T1CLK,
  output T2CLK,
  output T3CLK,
  output T4CLK,
  output [31:0] CPU_OUT,
  output [31:0] Memory_VALUE,
  output [23:0] Memory_ADDR,
  output WE,
  output OE,
  output CLK
);

  wire Add_out, ALUOP, ALUSTR, and_1_out, and_2_out, and_3_out, and_4_out, and_7_out, and_8_out, and_9_out,
       and_10_out, and_11_out, and_12_out, and_13_out, and_14_out, and_15_out, and_17_out, clock_1_out, CMP,
       CMP_out, controlled_buffer_2_out, controlled_buffer_39_out, controlled_buffer_40_out, d_ff_1_q,
       d_ff_2_q, d_ff_3_q, d_ff_4_q, EQ, GF_ALU, GS_ALU, HLT, JE, JG, JL, JMP, JNE, LDA, MODE_ENABLE, MOV_C,
       Mul_out, not_1_out, not_2_out, optcode_inent_1_nop_c, or_2_out, or_3_out, or_4_out, or_5_out,
       or_6_out, or_7_out, or_8_out, or_9_out, or_10_out, or_11_out, OUT_C, PRT0, PRT1, PRT2, PRT3, PRT4,
       PRT5, PRT6, PRT7, SRC_ENABLE, STR, Sub_out, undriven;
  wire [3:0] DEST_q, OPTCODE_q;
  wire [5:0] onehot_counter_1_out_4;
  wire [7:0] MAR_q, Register_Identifier_reg_out, Regsiter_identifier_reg_out;
  wire [23:0] controlled_buffer_1_out;
  wire [31:0] A_Reg_q, alu_16_1_out_7, B_Reg_q, controlled_buffer_3_out, controlled_buffer_4_out,
       controlled_buffer_5_out, controlled_buffer_6_out, controlled_buffer_7_out, controlled_buffer_8_out,
       controlled_buffer_9_out, controlled_buffer_10_out, controlled_buffer_11_out, controlled_buffer_12_out,
       controlled_buffer_37_out, controlled_buffer_38_out, JMP_ADDR_REG_q, R0_q, R1_q, R2_q, R3_q, R4_q,
       R5_q, R6_q, R7_q, SRC_q;
  wire [40:0] ram_1_dout;

  not not_1 (not_1_out, EQ);
  and and_1 (and_1_out, JE, EQ);
  and and_2 (and_2_out, JG, GF_ALU);
  and and_3 (and_3_out, JL, GS_ALU);
  and and_4 (and_4_out, JNE, not_1_out);
  D_Flip_Flop d_ff_1 (.D(and_1_out), .clk(T4CLK), .Q(d_ff_1_q), .reset(T1CLK));  // open: Qn, preset
  D_Flip_Flop d_ff_2 (.D(and_2_out), .clk(T4CLK), .Q(d_ff_2_q), .reset(T1CLK));  // open: Qn, preset
  D_Flip_Flop d_ff_3 (.D(and_3_out), .clk(T4CLK), .Q(d_ff_3_q), .reset(T1CLK));  // open: Qn, preset
  D_Flip_Flop d_ff_4 (.D(and_4_out), .clk(T4CLK), .Q(d_ff_4_q));  // open: Qn, preset, reset
  or u_CMP (CMP_out, d_ff_1_q, d_ff_2_q, d_ff_3_q, d_ff_4_q, JMP);
  assign controlled_buffer_1_out = Write_Enable ? ADDR : 24'bz;  // Controlled_Buffer controlled_buffer_1
  Clock clock_1 (.out(clock_1_out));
  Register #(.width(32)) JMP_ADDR_REG (
    .D(controlled_buffer_3_out), .en(CMP_out), .clk(T2CLK), .Q(JMP_ADDR_REG_q), .clr(undriven));
  buf and_5 (CLK, clock_1_out);  // AND_Gate
  assign controlled_buffer_2_out = T4CLK ? CMP_out : 1'bz;  // Controlled_Buffer controlled_buffer_2
  PC_Counter pc_counter_1 (
    .LOAD_DATA(controlled_buffer_2_out), .CLK(onehot_counter_1_out_4[5]), .DATA(JMP_ADDR_REG_q[31:8]),
    .CLR(PC_COUNTER_RST), .ADDR(controlled_buffer_1_out));
  OneHot_Counter onehot_counter_1 (
    .INT(CPU_INIT), .CLK(CLK), .RST(CPU_RST),
    .out_4({onehot_counter_1_out_4[5], T4CLK, T3CLK, T2CLK, T1CLK, onehot_counter_1_out_4[0]}));
  RAM #(.addrWidth(24), .dataWidth(41), .readbehav("war")) ram_1 (
    .addr(controlled_buffer_1_out), .we(Write_Enable), .oe(1'b1), .clk(CLK), .din(DATA), .dout(ram_1_dout));
  Register #(.width(4)) DEST (
    .D(ram_1_dout[7:4]), .en(onehot_counter_1_out_4[0]), .clk(onehot_counter_1_out_4[0]), .Q(DEST_q));  // open: clr
  not not_2 (not_2_out, MODE_ENABLE);
  Register #(.width(4)) OPTCODE (
    .D(ram_1_dout[3:0]), .en(onehot_counter_1_out_4[0]), .clk(onehot_counter_1_out_4[0]), .Q(OPTCODE_q));  // open: clr
  Register #(.width(1)) MODE (
    .D(ram_1_dout[8]), .en(onehot_counter_1_out_4[0]), .clk(onehot_counter_1_out_4[0]), .Q(MODE_ENABLE));  // open: clr
  Register #(.width(32)) SRC (
    .D(ram_1_dout[40:9]), .en(onehot_counter_1_out_4[0]), .clk(onehot_counter_1_out_4[0]), .Q(SRC_q));  // open: clr
  and and_6 (SRC_ENABLE, T1CLK, not_2_out);
  assign controlled_buffer_3_out = SRC_ENABLE ? SRC_q : 32'bz;  // Controlled_Buffer controlled_buffer_3
  REG_IDENT Regsiter_identifier (.REGSTER_NUM(DEST_q), .REG_OUT(Regsiter_identifier_reg_out));
  assign controlled_buffer_4_out = MODE_ENABLE ? SRC_q : 32'bz;  // Controlled_Buffer controlled_buffer_4
  REG_IDENT Register_Identifier (.REGSTER_NUM(controlled_buffer_4_out[3:0]), .REG_OUT(Register_Identifier_reg_out));
  OPTCODE_INENT optcode_inent_1 (
    .OPTCODE(OPTCODE_q), .STR_C(STR), .LDA_C(LDA), .JL_C(JL), .JG_C(JG), .JNE_C(JNE), .JE_C(JE), .CMP_C(CMP),
    .JMP_C(JMP), .HLT_C(HLT), .OUT_C(OUT_C), .MOV_C(MOV_C), .MUL_C(Mul_out), .SUB_C(Sub_out),
    .ADD_C(Add_out), .NOP_C(optcode_inent_1_nop_c));
  or or_1 (ALUOP, CMP, Sub_out, Add_out, Mul_out);
  or or_2 (or_2_out, T2CLK, and_7_out, ALUSTR);
  and and_7 (and_7_out, LDA, T4CLK);
  or or_3 (or_3_out, MOV_C, LDA, ALUSTR);
  and and_8 (and_8_out, or_2_out, or_3_out, Regsiter_identifier_reg_out[0]);
  or or_4 (or_4_out, MOV_C, LDA, ALUSTR);
  and and_9 (and_9_out, or_2_out, or_4_out, Regsiter_identifier_reg_out[1]);
  or or_5 (or_5_out, MOV_C, LDA, ALUSTR);
  and and_10 (and_10_out, or_2_out, or_5_out, Regsiter_identifier_reg_out[2]);
  or or_6 (or_6_out, MOV_C, LDA, ALUSTR);
  and and_11 (and_11_out, or_2_out, or_6_out, Regsiter_identifier_reg_out[3]);
  or or_7 (or_7_out, MOV_C, LDA, ALUSTR);
  and and_12 (and_12_out, or_2_out, or_7_out, Regsiter_identifier_reg_out[4]);
  or or_8 (or_8_out, MOV_C, LDA, ALUSTR);
  and and_13 (and_13_out, or_2_out, or_8_out, Regsiter_identifier_reg_out[5]);
  or or_9 (or_9_out, MOV_C, LDA, ALUSTR);
  and and_14 (and_14_out, or_2_out, or_9_out, Regsiter_identifier_reg_out[6]);
  or or_10 (or_10_out, MOV_C, LDA, ALUSTR);
  and and_15 (and_15_out, or_2_out, or_10_out, Regsiter_identifier_reg_out[7]);
  and and_16 (ALUSTR, T4CLK, ALUOP);
  Register #(.width(32)) R0 (.D(controlled_buffer_5_out), .en(and_8_out), .clk(and_8_out), .Q(R0_q), .clr(RESET_REG));
  assign controlled_buffer_5_out = CLK ? controlled_buffer_3_out : 32'bz;  // Controlled_Buffer controlled_buffer_5
  Register #(.width(32)) R1 (.D(controlled_buffer_6_out), .en(and_9_out), .clk(and_9_out), .Q(R1_q), .clr(RESET_REG));
  assign controlled_buffer_6_out = CLK ? controlled_buffer_3_out : 32'bz;  // Controlled_Buffer controlled_buffer_6
  Register #(.width(32)) R2 (.D(controlled_buffer_7_out), .en(and_10_out), .clk(and_10_out), .Q(R2_q), .clr(RESET_REG));
  assign controlled_buffer_7_out = CLK ? controlled_buffer_3_out : 32'bz;  // Controlled_Buffer controlled_buffer_7
  Register #(.width(32)) R3 (.D(controlled_buffer_8_out), .en(and_11_out), .clk(and_11_out), .Q(R3_q), .clr(RESET_REG));
  assign controlled_buffer_8_out = CLK ? controlled_buffer_3_out : 32'bz;  // Controlled_Buffer controlled_buffer_8
  Register #(.width(32)) R4 (.D(controlled_buffer_9_out), .en(and_12_out), .clk(and_12_out), .Q(R4_q), .clr(RESET_REG));
  assign controlled_buffer_9_out = CLK ? controlled_buffer_3_out : 32'bz;  // Controlled_Buffer controlled_buffer_9
  Register #(.width(32)) R5 (
    .D(controlled_buffer_10_out), .en(and_13_out), .clk(and_13_out), .Q(R5_q), .clr(RESET_REG));
  assign controlled_buffer_10_out = CLK ? controlled_buffer_3_out : 32'bz;  // Controlled_Buffer controlled_buffer_10
  Register #(.width(32)) R6 (
    .D(controlled_buffer_11_out), .en(and_14_out), .clk(and_14_out), .Q(R6_q), .clr(RESET_REG));
  assign controlled_buffer_11_out = CLK ? controlled_buffer_3_out : 32'bz;  // Controlled_Buffer controlled_buffer_11
  Register #(.width(32)) R7 (
    .D(controlled_buffer_12_out), .en(and_15_out), .clk(and_15_out), .Q(R7_q), .clr(RESET_REG));
  assign controlled_buffer_12_out = CLK ? controlled_buffer_3_out : 32'bz;  // Controlled_Buffer controlled_buffer_12
  assign PRT0 = T3CLK ? Regsiter_identifier_reg_out[0] : 1'bz;  // Controlled_Buffer controlled_buffer_13
  assign PRT1 = T3CLK ? Regsiter_identifier_reg_out[1] : 1'bz;  // Controlled_Buffer controlled_buffer_14
  assign PRT2 = T3CLK ? Regsiter_identifier_reg_out[2] : 1'bz;  // Controlled_Buffer controlled_buffer_15
  assign PRT3 = T3CLK ? Regsiter_identifier_reg_out[3] : 1'bz;  // Controlled_Buffer controlled_buffer_16
  assign PRT4 = T3CLK ? Regsiter_identifier_reg_out[4] : 1'bz;  // Controlled_Buffer controlled_buffer_17
  assign PRT5 = T3CLK ? Regsiter_identifier_reg_out[5] : 1'bz;  // Controlled_Buffer controlled_buffer_18
  assign PRT6 = T3CLK ? Regsiter_identifier_reg_out[6] : 1'bz;  // Controlled_Buffer controlled_buffer_19
  assign PRT7 = T3CLK ? Regsiter_identifier_reg_out[7] : 1'bz;  // Controlled_Buffer controlled_buffer_20
  assign controlled_buffer_3_out = PRT0 ? R0_q : 32'bz;  // Controlled_Buffer controlled_buffer_21
  assign controlled_buffer_3_out = PRT1 ? R1_q : 32'bz;  // Controlled_Buffer controlled_buffer_22
  assign controlled_buffer_3_out = PRT2 ? R2_q : 32'bz;  // Controlled_Buffer controlled_buffer_23
  assign controlled_buffer_3_out = PRT3 ? R3_q : 32'bz;  // Controlled_Buffer controlled_buffer_24
  assign controlled_buffer_3_out = PRT4 ? R4_q : 32'bz;  // Controlled_Buffer controlled_buffer_25
  assign controlled_buffer_3_out = PRT5 ? R5_q : 32'bz;  // Controlled_Buffer controlled_buffer_26
  assign controlled_buffer_3_out = PRT6 ? R6_q : 32'bz;  // Controlled_Buffer controlled_buffer_27
  assign controlled_buffer_3_out = PRT7 ? R7_q : 32'bz;  // Controlled_Buffer controlled_buffer_28
  assign PRT0 = T1CLK ? Register_Identifier_reg_out[0] : 1'bz;  // Controlled_Buffer controlled_buffer_29
  assign PRT1 = T1CLK ? Register_Identifier_reg_out[1] : 1'bz;  // Controlled_Buffer controlled_buffer_30
  assign PRT2 = T1CLK ? Register_Identifier_reg_out[2] : 1'bz;  // Controlled_Buffer controlled_buffer_31
  assign PRT3 = T1CLK ? Register_Identifier_reg_out[3] : 1'bz;  // Controlled_Buffer controlled_buffer_32
  assign PRT4 = T1CLK ? Register_Identifier_reg_out[4] : 1'bz;  // Controlled_Buffer controlled_buffer_33
  assign PRT5 = T1CLK ? Register_Identifier_reg_out[5] : 1'bz;  // Controlled_Buffer controlled_buffer_34
  assign PRT6 = T1CLK ? Register_Identifier_reg_out[6] : 1'bz;  // Controlled_Buffer controlled_buffer_35
  assign PRT7 = T1CLK ? Register_Identifier_reg_out[7] : 1'bz;  // Controlled_Buffer controlled_buffer_36
  assign controlled_buffer_37_out = T1CLK ? controlled_buffer_3_out : 32'bz;  // Controlled_Buffer controlled_buffer_37
  assign controlled_buffer_38_out = T3CLK ? controlled_buffer_3_out : 32'bz;  // Controlled_Buffer controlled_buffer_38
  assign controlled_buffer_39_out = T3CLK ? CLK : 1'bz;  // Controlled_Buffer controlled_buffer_39
  Register #(.width(32)) MDR (
    .D(controlled_buffer_3_out), .en(or_11_out), .clk(T4CLK), .Q(Memory_VALUE), .clr(RESET_REG));
  or or_11 (or_11_out, LDA, STR);
  Register #(.width(32)) MAR (
    .D(controlled_buffer_3_out), .en(STR), .clk(T2CLK), .Q({Memory_ADDR, MAR_q}), .clr(RESET_REG));
  Register #(.width(32)) A_Reg (
    .D(controlled_buffer_37_out), .en(ALUOP), .clk(controlled_buffer_40_out), .Q(A_Reg_q), .clr(RESET_REG));
  assign controlled_buffer_40_out = T1CLK ? CLK : 1'bz;  // Controlled_Buffer controlled_buffer_40
  Register #(.width(32)) B_Reg (
    .D(controlled_buffer_38_out), .en(ALUOP), .clk(controlled_buffer_39_out), .Q(B_Reg_q), .clr(RESET_REG));
  ALU_16 alu_16_1 (
    .in_1(A_Reg_q), .in_2(B_Reg_q), .ADD(Add_out), .SUB(Sub_out), .MUL(Mul_out), .CMP(CMP),
    .out_7(alu_16_1_out_7), .GREATER_FRST(GF_ALU), .EQUAL(EQ), .GREATER_SECOND(GS_ALU));
  assign controlled_buffer_3_out = T4CLK ? alu_16_1_out_7 : 32'bz;  // Controlled_Buffer controlled_buffer_41
  and and_17 (and_17_out, T4CLK, LDA);
  assign controlled_buffer_3_out = and_17_out ? MEM_OUT : 32'bz;  // Controlled_Buffer controlled_buffer_42
  Register #(.width(32)) register_1 (.D(controlled_buffer_3_out), .en(OUT_C), .clk(CLK), .Q(CPU_OUT));  // open: clr
  Hex_Digit_Display hex_digit_display_1 (.value(CPU_OUT[31:28]));  // open: dp
  Hex_Digit_Display hex_digit_display_2 (.value(CPU_OUT[27:24]));  // open: dp
  Hex_Digit_Display hex_digit_display_3 (.value(CPU_OUT[23:20]));  // open: dp
  Hex_Digit_Display hex_digit_display_4 (.value(CPU_OUT[19:16]));  // open: dp
  Hex_Digit_Display hex_digit_display_5 (.value(CPU_OUT[15:12]));  // open: dp
  Hex_Digit_Display hex_digit_display_6 (.value(CPU_OUT[11:8]));  // open: dp
  Hex_Digit_Display hex_digit_display_7 (.value(CPU_OUT[7:4]));  // open: dp
  Hex_Digit_Display hex_digit_display_8 (.value(CPU_OUT[3:0]));  // open: dp

  assign OE = 1'b1;
  assign WE = T4CLK;

  // Other names for the same wires on the sheet: MAIN_CLK = CLK

  // Notes on the sheet:
  //   Do Nothing
  //   Registers
  //   Main Clock
endmodule

module Sound_Card (
  input  in_1,
  input  in_2,
  input  [7:0] Memory_Out,
  input  [7:0] Memory_ADDR,
  output WE_OUT,
  output [13:0] Frequency,
  output [7:0] Volume
);

  wire and_1_out, and_2_out;
  wire [7:0] controlled_buffer_2_out;

  and and_1 (and_1_out, Memory_ADDR[4], Memory_ADDR[5], Memory_ADDR[2]);
  and and_2 (and_2_out, Memory_ADDR[4], Memory_ADDR[5], Memory_ADDR[0], Memory_ADDR[1]);
  assign Volume = and_1_out ? Memory_Out : 8'bz;  // Controlled_Buffer controlled_buffer_1
  assign controlled_buffer_2_out = and_2_out ? Memory_Out : 8'bz;  // Controlled_Buffer controlled_buffer_2
  Register register_1 (.D(controlled_buffer_2_out), .en(1'b1), .clk(in_2), .Q(Frequency[7:0]));  // open: clr

  assign Frequency[13:8] = {6{1'b0}};
  assign WE_OUT = in_1;

  // Other names for the same wires on the sheet: CLK = in_2; OE = in_1
endmodule

module VRAM (
  input  CHAR1,
  input  CHAR2,
  input  CLK_IN,
  input  WE_PORT_IN,
  input  RST_IN,
  input  [23:0] VALUE_IN,
  output RST,
  output CLK,
  output WE,
  output [8:0] X,
  output [8:0] Y,
  output [23:0] RGB
);

  wire counter_2_carry, or_1_out;
  wire [17:0] counter_1_q;

  or or_1 (or_1_out, CHAR1, CHAR2);
  Counter #(.max('h3ffff), .width(18)) counter_1 (
    .clr(RST_IN), .up(1'b1), .count(WE_PORT_IN), .clk(CLK_IN), .Q(counter_1_q));  // open: load, D, carry
  RAM #(.addrWidth(18), .dataWidth(24)) ram_1 (
    .addr(counter_1_q), .we(or_1_out), .oe(WE_PORT_IN), .clk(CLK_IN), .din(VALUE_IN), .dout(RGB));
  Counter #(.max('h1ff), .width(9)) counter_2 (
    .clr(RST_IN), .clk(CLK_IN), .carry(counter_2_carry), .Q(X));  // open: load, up, count, D
  Counter #(.max('h1ff), .width(9)) counter_3 (
    .clr(RST_IN), .clk(counter_2_carry), .Q(Y));  // open: load, up, count, D, carry

  assign CLK = CLK_IN;
  assign RST = RST_IN;
  assign WE = WE_PORT_IN;

  // Other names for the same wires on the sheet: CX[8:0] = X; CY[8:0] = Y; VRAM_WE = CHAR1; VRAM_WE1 = CHAR2;
  //   WE_PRT = WE_PORT_IN
endmodule

module OneHot_Counter_8 (
  input  INT,
  input  CLK,
  input  RST,
  output [7:0] out_4
);

  D_Flip_Flop d_ff_1 (.D(out_4[7]), .clk(CLK), .Q(out_4[0]), .preset(INT), .reset(RST));  // open: Qn
  D_Flip_Flop d_ff_2 (.D(out_4[0]), .clk(CLK), .Q(out_4[1]), .reset(RST));  // open: Qn, preset
  D_Flip_Flop d_ff_3 (.D(out_4[1]), .clk(CLK), .Q(out_4[2]), .reset(RST));  // open: Qn, preset
  D_Flip_Flop d_ff_4 (.D(out_4[2]), .clk(CLK), .Q(out_4[3]), .reset(RST));  // open: Qn, preset
  D_Flip_Flop d_ff_5 (.D(out_4[3]), .clk(CLK), .Q(out_4[4]));  // open: Qn, preset, reset
  D_Flip_Flop d_ff_6 (.D(out_4[4]), .clk(CLK), .Q(out_4[5]));  // open: Qn, preset, reset
  D_Flip_Flop d_ff_7 (.D(out_4[5]), .clk(CLK), .Q(out_4[6]));  // open: Qn, preset, reset
  D_Flip_Flop d_ff_8 (.D(out_4[6]), .clk(CLK), .Q(out_4[7]));  // open: Qn, preset, reset
endmodule

module ALU_16 (
  input  [31:0] in_1,
  input  [31:0] in_2,
  input  ADD,
  input  SUB,
  input  MUL,
  input  CMP,
  output [31:0] out_7,
  output GREATER_FRST,
  output EQUAL,
  output GREATER_SECOND
);

  wire comparator_1_eq, comparator_1_gt, comparator_1_lt;
  wire [31:0] adder_1_out, multiplier_1_out, subtractor_1_out;

  Adder #(.width(32)) adder_1 (.a(in_1), .b(in_2), .out(adder_1_out));  // open: cin, cout
  Subtractor #(.width(32)) subtractor_1 (.a(in_1), .b(in_2), .out(subtractor_1_out));  // open: bin, bout
  Multiplier #(.width(32)) multiplier_1 (.a(in_1), .b(in_2), .out(multiplier_1_out));  // open: cin, cout
  Comparator #(.mode("unsigned"), .width(32)) comparator_1 (
    .a(in_1), .b(in_2), .gt(comparator_1_gt), .eq(comparator_1_eq), .lt(comparator_1_lt));
  assign out_7 = ADD ? adder_1_out : 32'bz;  // Controlled_Buffer controlled_buffer_1
  assign out_7 = SUB ? subtractor_1_out : 32'bz;  // Controlled_Buffer controlled_buffer_2
  assign GREATER_FRST = CMP ? comparator_1_gt : 1'bz;  // Controlled_Buffer controlled_buffer_3
  assign EQUAL = CMP ? comparator_1_eq : 1'bz;  // Controlled_Buffer controlled_buffer_4
  assign GREATER_SECOND = CMP ? comparator_1_lt : 1'bz;  // Controlled_Buffer controlled_buffer_5
  assign out_7 = MUL ? multiplier_1_out : 32'bz;  // Controlled_Buffer controlled_buffer_6
endmodule

module CharacterWriter (
  input  CLK,
  input  RST,
  input  [8:0] CX,
  input  [8:0] CY,
  input  [8:0] UX,
  input  [8:0] UY,
  input  [7:0] Letter,
  input  [23:0] BG,
  input  [23:0] FG,
  output [23:0] VALUE_OUT,
  output CHAR1,
  output CHAR2
);

  wire and_1_out, and_2_out, comparator_1_eq, comparator_2_eq, comparator_3_eq, comparator_4_eq,
       comparator_5_eq, comparator_6_eq, comparator_7_eq, comparator_8_eq, comparator_9_eq, comparator_10_eq,
       comparator_11_eq, controlled_buffer_1_out, multiplexer_1_out, or_1_out, or_2_out;
  wire [2:0] SX_q, SY_q;
  wire [7:0] adder_1_out, rom_1_data;
  wire [8:0] adder_2_out, adder_3_out, adder_4_out, adder_5_out, adder_6_out, adder_7_out, adder_8_out,
       adder_9_out;

  Counter #(.max('h7), .width(3)) SY (
    .clr(RST), .up(1'b1), .count(1'b1), .clk(and_1_out), .Q(SY_q));  // open: load, D, carry
  ROM rom_1 (.addr(adder_1_out), .data(rom_1_data));
  Adder adder_1 (.a({{5{1'b0}}, SY_q}), .b(Letter), .out(adder_1_out));  // open: cin, cout
  or or_1 (or_1_out, CHAR1, CHAR2);
  Counter #(.max('h7), .width(3)) SX (
    .clr(RST), .up(or_1_out), .count(or_1_out), .clk(CLK), .Q(SX_q));  // open: load, D, carry
  Multiplexer #(.select(3)) multiplexer_1 (
    .in0(rom_1_data[0]), .in1(rom_1_data[1]), .in2(rom_1_data[2]), .in3(rom_1_data[3]), .in4(rom_1_data[4]),
    .in5(rom_1_data[5]), .in6(rom_1_data[6]), .in7(rom_1_data[7]), .out(multiplexer_1_out), .sel(SX_q));
  Multiplexer #(.width(24)) multiplexer_2 (.in0(BG), .in1(FG), .out(VALUE_OUT), .sel(multiplexer_1_out));
  and and_1 (and_1_out, SX_q[0], SX_q[1], SX_q[2]);
  Comparator #(.mode("unsigned"), .width(9)) comparator_1 (.a(UX), .b(CX), .eq(comparator_1_eq));  // open: gt, lt
  Comparator #(.mode("unsigned"), .width(9)) comparator_2 (.a(UY), .b(CY), .eq(comparator_2_eq));  // open: gt, lt
  Adder #(.width(9)) adder_2 (.a(UY), .b(9'h1), .out(adder_2_out));  // open: cin, cout
  Adder #(.width(9)) adder_3 (.a(UY), .b(9'h2), .out(adder_3_out));  // open: cin, cout
  Adder #(.width(9)) adder_4 (.a(UY), .b(9'h3), .out(adder_4_out));  // open: cin, cout
  Adder #(.width(9)) adder_5 (.a(UY), .b(9'h4), .out(adder_5_out));  // open: cin, cout
  Adder #(.width(9)) adder_6 (.a(UY), .b(9'h5), .out(adder_6_out));  // open: cin, cout
  Adder #(.width(9)) adder_7 (.a(UY), .b(9'h6), .out(adder_7_out));  // open: cin, cout
  Adder #(.width(9)) adder_8 (.a(UY), .b(9'h7), .out(adder_8_out));  // open: cin, cout
  Comparator #(.mode("unsigned"), .width(9)) comparator_3 (.a(UX), .b(CX), .eq(comparator_3_eq));  // open: gt, lt
  Comparator #(.mode("unsigned"), .width(9)) comparator_4 (
    .a(adder_2_out), .b(CY), .eq(comparator_4_eq));  // open: gt, lt
  Comparator #(.mode("unsigned"), .width(9)) comparator_5 (
    .a(adder_3_out), .b(CY), .eq(comparator_5_eq));  // open: gt, lt
  Comparator #(.mode("unsigned"), .width(9)) comparator_6 (
    .a(adder_4_out), .b(CY), .eq(comparator_6_eq));  // open: gt, lt
  Comparator #(.mode("unsigned"), .width(9)) comparator_7 (
    .a(adder_5_out), .b(CY), .eq(comparator_7_eq));  // open: gt, lt
  Comparator #(.mode("unsigned"), .width(9)) comparator_8 (
    .a(adder_6_out), .b(CY), .eq(comparator_8_eq));  // open: gt, lt
  Comparator #(.mode("unsigned"), .width(9)) comparator_9 (
    .a(adder_7_out), .b(CY), .eq(comparator_9_eq));  // open: gt, lt
  Comparator #(.mode("unsigned"), .width(9)) comparator_10 (
    .a(adder_8_out), .b(CY), .eq(comparator_10_eq));  // open: gt, lt
  and and_2 (and_2_out, comparator_1_eq, comparator_2_eq);
  T_Flip_Flop t_ff_1 (.T(and_2_out), .clk(and_2_out), .Q(CHAR1), .reset(comparator_11_eq));  // open: Qn, preset
  or or_2 (or_2_out, comparator_4_eq, comparator_5_eq, comparator_6_eq, comparator_7_eq, comparator_8_eq, comparator_9_eq, comparator_10_eq);
  assign controlled_buffer_1_out = comparator_3_eq ? or_2_out : 1'bz;  // Controlled_Buffer controlled_buffer_1
  Adder #(.width(9)) adder_9 (.a(UX), .b(9'h8), .out(adder_9_out));  // open: cin, cout
  Pull_Resistor pull_resistor_1 (.node(controlled_buffer_1_out));
  Comparator #(.mode("unsigned"), .width(9)) comparator_11 (
    .a(adder_9_out), .b(CX), .eq(comparator_11_eq));  // open: gt, lt
  T_Flip_Flop t_ff_2 (
    .T(controlled_buffer_1_out), .clk(controlled_buffer_1_out), .Q(CHAR2), .reset(comparator_11_eq));  // open: Qn, preset

  // Other names for the same wires on the sheet: LET[7:0] = Letter; VRAM_WE = CHAR1; VRAM_WE1 = CHAR2

  // Notes on the sheet:
  //   contents of rom_1 (hex, n*v repeats v):
  //   1c 22 22 3e 22 22 22 0 1e 22 22 1e 22 22 1e 0 8*ff
endmodule
